// Digital circuit 2layerCir.dig as structural Verilog
module _2layerCir (
  input  a,
  input  b,
  input  c,
  input  d,
  output f,
  output g
);

  wire and_1_out, and_2_out, and_3_out, and_4_out, and_5_out, and_6_out, not_1_out, not_2_out, not_3_out;

  not not_1 (not_1_out, b);
  not not_2 (not_2_out, c);
  not not_3 (not_3_out, a);
  and and_1 (and_1_out, a, ~b, ~c);  // And
  and and_2 (and_2_out, a, c, ~d);  // And
  and and_3 (and_3_out, not_3_out, not_1_out, d);
  and and_4 (and_4_out, not_2_out, d);
  and and_5 (and_5_out, ~a, b);  // And
  and and_6 (and_6_out, b, ~c, d);  // And
  or or_1 (f, and_1_out, and_2_out, and_3_out, and_4_out);
  or or_2 (g, and_2_out, and_5_out, and_6_out);
endmodule
