// Digital circuit alarm_system.dig as structural Verilog
module alarm_system (
  input  s1,
  input  s2,
  input  s3,
  input  s4,
  input  m,
  input  a,
  input  L,
  input  p,
  input  in_12,
  input  in_13,
  input  in_14,
  input  in_16,
  input  in_17,
  input  in_18,
  input  in_19,
  input  in_20,
  input  in_21,
  input  in_22,
  input  in_23,
  output B,
  output F,
  output C,
  output out_15,
  output out_24
);

  wire and_1_out, and_2_out, and_3_out, and_4_out, not_1_out, not_2_out, not_3_out, not_4_out, or_1_out,
       or_2_out, or_3_out, xor_1_out, xor_2_out, xor_3_out, xor_4_out, xor_5_out, xor_6_out, xor_7_out,
       xor_8_out, xor_10_out;

  or or_1 (or_1_out, s1, s2);
  or or_2 (or_2_out, s3, s4);
  or or_3 (or_3_out, or_1_out, or_2_out);
  and and_1 (and_1_out, in_14, in_12);
  and and_2 (and_2_out, in_12, in_13);
  and and_3 (and_3_out, in_13, in_14);
  not not_1 (not_1_out, m);
  or or_4 (out_15, and_1_out, and_3_out);
  and and_4 (and_4_out, or_3_out, not_1_out);
  and and_5 (B, a, and_4_out);
  and and_6 (F, and_4_out, L);
  and and_7 (C, and_4_out, p);
  xor xor_1 (xor_1_out, in_18, in_16);
  xor xor_2 (xor_2_out, in_16, in_17);
  xor xor_3 (xor_3_out, in_18, in_19);
  xor xor_4 (xor_4_out, in_17, in_19);
  xor xor_5 (xor_5_out, in_20, in_21);
  xor xor_6 (xor_6_out, in_22, in_23);
  not not_2 (not_2_out, xor_2_out);
  xor xor_7 (xor_7_out, xor_1_out, not_2_out);
  xor xor_8 (xor_8_out, xor_3_out, xor_4_out);
  xor xor_9 (out_24, xor_5_out, xor_6_out);
  not not_3 (not_3_out, xor_7_out);
  not not_4 (not_4_out, xor_8_out);
  xor xor_10 (xor_10_out, not_3_out, not_4_out);
endmodule
