// Digital circuit base-12-counter.dig as structural Verilog
module base_12_counter (
  input  in_1,
  input  q0,
  input  q1,
  input  q2,
  input  q3,
  output q0_plus,
  output q1_plus,
  output q2_plus,
  output q3_plus
);

  D_FF d_ff_1 (.D(q0), .C(in_1), .Q(q0_plus));  // open: nQ
  D_FF d_ff_2 (.D(q1), .C(in_1), .Q(q1_plus));  // open: nQ
  D_FF d_ff_3 (.D(q2), .C(in_1), .Q(q2_plus));  // open: nQ
  D_FF d_ff_4 (.D(q3), .C(in_1), .Q(q3_plus));  // open: nQ
endmodule
