// Digital circuit dflip.dig as structural Verilog
module dflip (
  input  a,
  input  b,
  input  x,
  input  clk,
  input  b_2,
  input  c,
  output out_7
);

  wire and_1_out, and_2_out, and_3_out, and_4_out, and_5_out, and_6_out, not_1_out, not_2_out, not_3_out,
       or_1_out, or_2_out;

  not not_1 (not_1_out, a);
  not not_2 (not_2_out, b);
  not not_3 (not_3_out, a);
  and and_1 (and_1_out, not_1_out, not_2_out);
  and and_2 (and_2_out, not_2_out, x);
  and and_3 (and_3_out, a, not_2_out);
  and and_4 (and_4_out, not_3_out, x);
  or or_1 (or_1_out, and_1_out, and_2_out);
  or or_2 (or_2_out, and_3_out, and_4_out);
  D_FF d_ff_1 (.D(or_2_out), .C(clk), .Q(b_2));  // open: nQ
  D_FF d_ff_2 (.D(or_1_out), .C(clk), .Q(a));  // open: nQ
  buf and_5 (and_5_out, a);  // And open: In_2
  and and_6 (and_6_out, b_2, a);
  or or_3 (out_7, and_5_out, and_6_out);
endmodule
