// Digital circuit scale.dig as structural Verilog
module scale (
  input  W_1,
  input  W_2,
  input  clk,
  input  reset,
  output L,
  output R,
  output E
);

  wire and_1_out, and_2_out, and_3_out, and_4_out, and_5_out, and_6_out, and_7_out, and_8_out, and_9_out,
       and_10_out, and_11_out, and_12_out, and_13_out, and_14_out, and_15_out, and_16_out, and_17_out,
       and_18_out, or_1_out, or_2_out, or_3_out, or_4_out, q1, q1_t, q2, q2_t, q3, q3_t, q3_t_t, w1_t, w2_t;

  not not_1 (w1_t, W_1);
  not not_2 (w2_t, W_2);
  and and_1 (and_1_out, q1, q2_t, q3);
  and and_2 (and_2_out, q1, q2_t, w1_t);
  and and_3 (and_3_out, q2, q3, w1_t, W_2);
  and and_4 (and_4_out, q2, q3_t, W_1, w2_t);
  and and_5 (and_5_out, q2, w2_t, w1_t);
  and and_6 (and_6_out, q1, q3_t, W_1);
  and and_7 (and_7_out, q1_t, q2_t, q3, W_1, w2_t);
  and and_8 (and_8_out, q1_t, q2_t, q3_t, w1_t, W_2);
  and and_9 (and_9_out, w2_t, w1_t, q3);
  and and_10 (and_10_out, q2, q3_t, W_2);
  and and_11 (and_11_out, q3_t, W_1, w2_t);
  and and_12 (and_12_out, q3_t, w1_t, W_2);
  and and_13 (and_13_out, q1, q2_t, W_2);
  and and_14 (and_14_out, q1, q2_t, W_1);
  or or_1 (or_1_out, and_9_out, and_10_out, and_11_out);
  or or_2 (or_2_out, and_12_out, and_13_out, and_14_out);
  or or_3 (or_3_out, and_1_out, and_2_out, and_3_out, and_4_out);
  or or_4 (or_4_out, and_5_out, and_6_out, and_7_out, and_8_out);
  or or_5 (q3_t_t, or_1_out, or_2_out);
  D_FF_AS u_q1 (.Set(1'b0), .D(or_3_out), .C(clk), .Clr(reset), .Q(q1), .nQ(q1_t));
  D_FF_AS u_q2 (.Set(1'b0), .D(or_4_out), .C(clk), .Clr(reset), .Q(q2), .nQ(q2_t));
  D_FF_AS u_q3 (.Set(1'b0), .D(q3_t_t), .C(clk), .Clr(reset), .Q(q3), .nQ(q3_t));
  and and_15 (and_15_out, q1_t, q2_t, q3);
  and and_16 (and_16_out, q2, q3_t);
  and and_17 (and_17_out, q1, q3_t);
  and and_18 (and_18_out, q2, q3);
  and and_19 (E, q1, q2_t, q3);
  or or_6 (L, and_15_out, and_16_out);
  or or_7 (R, and_17_out, and_18_out);

  // Other names for the same wires on the sheet: w1 = W_1; w2 = W_2
endmodule
