// Digital circuit jk.dig as structural Verilog
module jk (
  input  B,
  input  A,
  input  X,
  input  in_4,
  input  c,
  output z
);

  wire and_1_out, and_2_out, jk_ff_1_q, jk_ff_2_q, not_1_out, not_2_out, not_3_out, or_1_out, or_2_out,
       undriven;

  not not_1 (not_1_out, B);
  or or_1 (or_1_out, A, X);
  or or_2 (or_2_out, A, not_2_out);
  not not_2 (not_2_out, X);
  JK_FF jk_ff_1 (.J(not_1_out), .C(undriven), .K(in_4), .Q(jk_ff_1_q));  // open: nQ
  JK_FF jk_ff_2 (.J(or_1_out), .C(undriven), .K(or_2_out), .Q(jk_ff_2_q));  // open: nQ
  not not_3 (not_3_out, c);
  and and_1 (and_1_out, jk_ff_1_q, not_3_out);
  and and_2 (and_2_out, jk_ff_2_q, A);
  or or_3 (z, and_1_out, and_2_out);

  // Notes on the sheet:
  //   in_4: pin 1, default 1
endmodule
