// Digital circuit four_bit_mux_display.dig as structural Verilog
module four_bit_mux_display (
  input  [3:0] a,
  input  [3:0] b,
  input  sel,
  output [3:0] y
);

  Seven_Seg_Hex seven_seg_hex_1 (.d(a), .dp(1'b0));
  Seven_Seg_Hex seven_seg_hex_2 (.d(b), .dp(1'b0));
  // two_bit_mux two_bit_mux_1: pin names not known; wires that end beside it: a[3], b[3], sel, y[3]
  // two_bit_mux two_bit_mux_2: pin names not known; wires that end beside it: a[2], b[2], sel, y[2]
  // two_bit_mux two_bit_mux_3: pin names not known; wires that end beside it: a[1], b[1], sel, y[1]
  // two_bit_mux two_bit_mux_4: pin names not known; wires that end beside it: a[0], b[0], sel, y[0]
  Seven_Seg_Hex seven_seg_hex_3 (.d(y), .dp(1'b0));
endmodule
