// Digital circuit not_neg.dig as structural Verilog
module not_neg (
  input  [3:0] a,
  input  inv,
  input  neg,
  output [3:0] y,
  output cry
);

  wire and_1_out;
  wire [3:0] xor_1_out;

  xor xor_1 (xor_1_out[3], inv, a[3]);
  xor xor_2 (xor_1_out[2], inv, a[2]);
  xor xor_3 (xor_1_out[1], inv, a[1]);
  xor xor_4 (xor_1_out[0], inv, a[0]);
  and and_1 (and_1_out, inv, neg);
  incrementer incrementer_1 (.a(xor_1_out), .inc(and_1_out), .cry(cry), .y(y));
endmodule
