// Digital circuit program_ctr.dig as structural Verilog
module program_ctr (
  input  enable,
  input  reset,
  input  clk,
  output [3:0] q
);

  wire [3:0] incrementer_1_y;

  incrementer incrementer_1 (.a(q), .inc(1'b1), .y(incrementer_1_y));  // open: cry
  four_bit_reg four_bit_reg_1 (.d(incrementer_1_y), .enable(enable), .reset(reset), .clk(clk), .q(q));
endmodule
