// Digital circuit two_bit_bus_mux.dig as structural Verilog
module two_bit_bus_mux (
  input  [1:0] a,
  input  [1:0] b,
  input  sel,
  output [1:0] y
);

  // two_bit_mux two_bit_mux_1: pin names not known; wires that end beside it: a[1], b[1], sel, y[1]
  // two_bit_mux two_bit_mux_2: pin names not known; wires that end beside it: a[0], b[0], sel, y[0]
endmodule
