// Digital circuit two_bit_mux.dig as structural Verilog
module two_bit_mux (
  input  [3:0] a,
  input  [3:0] b,
  input  [3:0] s,
  output [3:0] y
);

  wire and_1_out, and_2_out, not_1_out;

  not not_1 (not_1_out, s[0]);
  and and_1 (and_1_out, a[0], not_1_out);
  and and_2 (and_2_out, b[0], s[0]);
  or or_1 (y[0], and_1_out, and_2_out);
  // Pins of 1 and 4 bits meet at a
  // Pins of 1 and 4 bits meet at b
  // Pins of 1 and 4 bits meet at s
  // Pins of 1 and 4 bits meet at y
endmodule
